# Fritzing sketch minigames (saved by Fritzing 1.0.6)
breadboards: 1

parts:
  Part1 = Adafruit ESP32 Feather V2
  LED1 = LED - 5mm [color="Red (633nm)" current=0.030A package="5 mm [THT]"]
  LED2 = LED - 5mm [color="Yellow (585nm)" current=0.030A package="5 mm [THT]"]
  LED3 = LED - 5mm [color="Green (555nm)" current=0.030A package="5 mm [THT]"]
  S1 = Pushbutton [package="[THT]"]
  S2 = Pushbutton [package="[THT]"]
  R1 = Resistor [tolerance=±5% power=0.25W resistance=220 package=THT]
  R2 = Resistor [tolerance=±5% power=0.25W resistance=220 package=THT]
  S3 = Pushbutton [package="[THT]"]
  R3 = Resistor [tolerance=±5% power=0.25W resistance=220 package=THT]
  Part2 = LCD1602-I2C
  R4 = TRIMPOT [maximum_resistance=10kΩ knob_status=50% power=0.5W package=3386u]
  J2 = Buzzer
  Q1 = NPN-Transistor [package="TO92 [THT]"]
  R5 = Resistor [tolerance=±5% power=0.25W resistance=1k package=THT]

nets:
  N1: Part1.SDA, Part1.IO27_A10, LED3.cathode, Part2.SDA
  N2: Part1.A2_I34, R4.WIPER
  GND: Part1.GND, R1.Pin_1, R2.Pin_1, R3.Pin_1, Part2.GND, R4.CW, Q1.C
  3.3V: Part1.3.3V, Part2.VCC, R4.CCW, J2.pin1, J2.pin2, Q1.E
  N3: Part1.IO12_A11, LED1.cathode
  N4: Part1.IO33_A9, LED2.cathode
  N5: Part1.IO32_A7, R5.Pin_1
  N6: Part1.SCL, Part2.SCL
  N7: LED1.anode, S1.Pin_3, S1.Pin_4
  N8: LED2.anode, S3.Pin_3, S3.Pin_4
  N9: LED3.anode, S2.Pin_3, S2.Pin_4
  N10: S1.Pin_1, S1.Pin_2, R1.Pin_0
  N11: S2.Pin_1, S2.Pin_2, R2.Pin_0
  N12: S3.Pin_1, S3.Pin_2, R3.Pin_0
  N13: Q1.B, R5.Pin_0

notes:
  GPIO32 PWM ADC1_CH4 -> NPN Base
  SCL -> SCL
  SDA -> SDA
  POT -> GPIO34 ADC1_CH6
  GPIO33 -> YELLOW
  GPIO27 -> GREEN
  GPIO12 -> RED
  Wire color Legend:
  VCC - Red
  GND - Black
  Data - Blue
  ADC/PWM - Orange
  SCL - Green
  SDA - Yellow

custom parts:
  LCD1602-I2C: A standard character display, usually with 2x16 characters. Comes in many colors with LCM1602 IIC attached.
  Buzzer: Fixed frequency buzzer
